# Fritzing sketch TB2-Dev-Board-Rev1.0 (saved by Fritzing 1.0.8)

parts:
  JZ1 = JZ1 Flipper 2-8 / 1x7 [value="Flipper 2-8 / 1x7" part_number=PZ254V-11-07P package=PZ254V-11-07P]
  JZ2 = JZ2 Flipper 9-11 / 1x3 [value="Flipper 9-11 / 1x3" part_number=PZ254V-11-03P package=PZ254V-11-03P]
  J1 = J1 SOP8-Clip (Chip-Pins) [value="SOP8-Clip (Chip-Pins)" part_number=61200821621 package=61200821621]
  S1 = S1 POWER / rastend [value="POWER / rastend" part_number=K3-1296S-E1 package=K3-1296S-E1]
  S2 = S2 RESET / ALPS SKRPACE010 [value="RESET / ALPS SKRPACE010" part_number=SKRPACE010 package=SKRPACE010]
  R1 = R1 1 kOhm [value="1 kOhm" part_number=RC0603FR-071KL package=RC0603FR-071KL]
  D1 = D1 POWER / GRUEN [value="POWER / GRUEN" part_number=APH1608SGC package=APH1608SGC]
  R5 = R5 10 kOhm / CS-Pull-up [value="10 kOhm / CS-Pull-up" part_number=RC0603FR-0710KL package=RC0603FR-0710KL]
  R6 = R6 100 kOhm / Nachlauf [value="100 kOhm / Nachlauf" part_number=RC0603FR-07100KL package=RC0603FR-07100KL]
  C2 = C2 1 uF / X7R [value="1 uF / X7R" part_number=GRM21BR71A105KA01L package=GRM21BR71A105KA01L]
  C1 = C1 100 nF / U1 [value="100 nF / U1" part_number=GRM188R71C104KA01D package=GRM188R71C104KA01D]
  R7 = R7 560 kOhm / Blinktakt [value="560 kOhm / Blinktakt" part_number=RC0603FR-07560KL package=RC0603FR-07560KL]
  C3 = C3 1 uF / X7R [value="1 uF / X7R" part_number=GRM21BR71A105KA01L package=GRM21BR71A105KA01L]
  C4 = C4 100 nF / U2 [value="100 nF / U2" part_number=GRM188R71C104KA01D package=GRM188R71C104KA01D]
  R2 = R2 1 kOhm [value="1 kOhm" part_number=RC0603FR-071KL package=RC0603FR-071KL]
  D2 = D2 ACCESS / ROT [value="ACCESS / ROT" part_number=APT1608SURCK package=APT1608SURCK]
  U1 = U1 SN74LVC1G123DCTR [value=SN74LVC1G123DCTR part_number=SN74LVC1G123DCTR package=SN74LVC1G123DCTR]
  U2 = U2 SN74LVC1G132DCKR [value=SN74LVC1G132DCKR part_number=SN74LVC1G132DCKR package=SN74LVC1G132DCKR]
  Q1 = Q1 AO3401A / P-MOS [value="AO3401A / P-MOS" part_number=AO3401A package=AO3401A]
  R8 = R8 100k / Gate pulldown [value="100k / Gate pulldown" part_number=RC0603FR-07100KL package=RC0603FR-07100KL]
  R9 = R9 1k / Gate series [value="1k / Gate series" part_number=RC0603FR-071KL package=RC0603FR-071KL]
  R10 = R10 4.7k / POWER LED shunt [value="4.7k / POWER LED shunt" part_number=RC0603FR-074K7L package=RC0603FR-074K7L]
  MARK1 = FRONT orientation  # not connected
  MARK2 = FLIPPER / TB2 DEV  # not connected
  MARK3 = Netfreak  # not connected

nets:
  N1: JZ1.2_MOSI, J1.5_MOSI
  N2: JZ1.3_MISO, J1.2_MISO
  N3: JZ1.4_CS, J1.1_/CS, R5.1, U1.1_A_/CS
  N4: JZ1.5_CLK, J1.6_CLK, U1.2_B_CLK
  N5: JZ2.9_3V3_IN, S1.1
  N6: JZ2.11_GND, J1.4_GND, S1.NC_unused_physical_housing1, S1.NC_unused_physical_housing2, S1.NC_unused_physical_housing3, S1.NC_unused_physical_housing4, D1.K, C1.2, C3.2, C4.2, U1.4_GND, U2.3_GND, R8.2, R10.2
  N7: J1.3_/WP, J1.7_/HOLD, J1.8_VCC, R1.1, R5.2, R6.1, C1.1, C4.1, R2.1, U1.3_/CLR, U1.8_VCC, U2.5_VCC, Q1.3_D
  N8: S1.2, S2.1_/_source, S2.4_/_source, Q1.2_S
  N9: S2.2_/_gate_R9, S2.3_/_gate_R9, R9.1
  N10: R1.2, D1.A, R10.1
  N11: R6.2, C2.2, U1.7_Rext/Cext
  N12: C2.1, U1.6_Cext
  N13: R7.1, D2.K, U2.4_Y
  N14: R7.2, C3.1, U2.2_B
  N15: R2.2, D2.A
  N16: U1.5_Q, U2.1_A
  N17: Q1.1_G, R8.1, R9.2

notes:
  VERBUNDENER SCHALTPLAN
  Alle Netze sind durch echte Leitungen verbunden. Punkte: Verbindung. Kreuzungen ohne Punkt: keine Verbindung.
  S2 schliesst beim Druecken und sperrt Q1. R8 schaltet Q1 beim Loslassen ein. J1-Ziffern = Chip-Pins.

custom parts:
  JZ1 Flipper 2-8 / 1x7: Manufacturer land pattern: XFCN PZ254V-11-07P. 6.1 +/-0.2 mm mating pins DOWN; 0.64 mm square; 3 mm solder tails
  JZ2 Flipper 9-11 / 1x3: Manufacturer land pattern: XFCN PZ254V-11-03P. 6.1 +/-0.2 mm mating pins DOWN; 0.64 mm square; 3 mm solder tails
  J1 SOP8-Clip (Chip-Pins): Manufacturer land pattern: Wuerth Elektronik 61200821621. Notch LEFT; CHIP1 upper-left; manufacturer pad1 = CHIP1; 90 deg clockwise from notch-down reference; reference geometry pending supplier selection
  S1 POWER / rastend: Manufacturer land pattern: Hroparts K3-1296S-E1. SMD; actuator UP; two 0.9 mm NPTH locating holes; housing tabs GND
  S2 RESET / ALPS SKRPACE010: Manufacturer land pattern: ALPS Alpine SKRPACE010. ALPS physical 1-2 source; 3-4 reset contact; 2.5 mm high; NO
  R1 1 kOhm: Manufacturer land pattern: Yageo RC0603FR-071KL.
  D1 POWER / GRUEN: Manufacturer land pattern: Kingbright APH1608SGC. Manufacturer pin2 / anode LEFT; pin1 / cathode RIGHT, K bar on silkscreen
  R5 10 kOhm / CS-Pull-up: Manufacturer land pattern: Yageo RC0603FR-0710KL.
  R6 100 kOhm / Nachlauf: Manufacturer land pattern: Yageo RC0603FR-07100KL.
  C2 1 uF / X7R: Manufacturer land pattern: Murata GRM21BR71A105KA01L.
  C1 100 nF / U1: Manufacturer land pattern: Murata GRM188R71C104KA01D.
  R7 560 kOhm / Blinktakt: Manufacturer land pattern: Yageo RC0603FR-07560KL.
  C3 1 uF / X7R: Manufacturer land pattern: Murata GRM21BR71A105KA01L.
  C4 100 nF / U2: Manufacturer land pattern: Murata GRM188R71C104KA01D.
  R2 1 kOhm: Manufacturer land pattern: Yageo RC0603FR-071KL.
  D2 ACCESS / ROT: Manufacturer land pattern: Kingbright APT1608SURCK. Manufacturer pin2 / anode LEFT; pin1 / cathode RIGHT, K bar on silkscreen
  U1 SN74LVC1G123DCTR: Manufacturer land pattern: Texas Instruments SN74LVC1G123DCTR.
  U2 SN74LVC1G132DCKR: Manufacturer land pattern: Texas Instruments SN74LVC1G132DCKR.
  Q1 AO3401A / P-MOS: Manufacturer land pattern: Alpha and Omega Semiconductor AO3401A. P-channel high-side switch; source upstream, drain TARGET; pin1 dot lower-left
  R8 100k / Gate pulldown: Manufacturer land pattern: Yageo RC0603FR-07100KL.
  R9 1k / Gate series: Manufacturer land pattern: Yageo RC0603FR-071KL.
  R10 4.7k / POWER LED shunt: Manufacturer land pattern: Yageo RC0603FR-074K7L.
  FRONT orientation: silkscreen only; no assembly item
  FLIPPER / TB2 DEV: silkscreen only; no assembly item
  Netfreak: silkscreen0 only; no assembly item
